# Fritzing sketch esquema (saved by Fritzing 0.9.3b)
breadboards: 1

parts:
  Componente2 = Arduino Mega ADK (Rev3)
  SW1 = DIP Switch 8 Position [package=dipswitch-08]
  SW2 = DIP Switch 8 Position [package=dipswitch-08]
  R1 = Resistor [tolerance=±5% resistance=220 package="0805 [SMD]"]
  R2 = Resistor [tolerance=±5% resistance=220 package="0805 [SMD]"]
  R3 = Resistor [tolerance=±5% resistance=220 package="0805 [SMD]"]
  R4 = Resistor [tolerance=±5% resistance=220 package="0805 [SMD]"]
  R5 = Resistor [tolerance=±5% resistance=220 package="0805 [SMD]"]
  R6 = Resistor [tolerance=±5% resistance=220 package="0805 [SMD]"]
  R7 = Resistor [tolerance=±5% resistance=220 package="0805 [SMD]"]
  R8 = Resistor [tolerance=±5% resistance=220 package="0805 [SMD]"]
  R9 = Resistor [tolerance=±5% resistance=220 package="0805 [SMD]"]
  R10 = Resistor [tolerance=±5% resistance=220 package="0805 [SMD]"]
  R11 = Resistor [tolerance=±5% resistance=220 package="0805 [SMD]"]
  R12 = Resistor [tolerance=±5% resistance=220 package="0805 [SMD]"]
  R13 = Resistor [tolerance=±5% resistance=220 package="0805 [SMD]"]
  LED1 = smd LED [color="Red (633nm)" package="0805 [SMD]"]
  LED2 = smd LED [color="Red (633nm)" package="0805 [SMD]"]
  LED3 = smd LED [color="Red (633nm)" package="0805 [SMD]"]
  LED4 = smd LED [color="Red (633nm)" package="0805 [SMD]"]
  LED5 = smd LED [color="Red (633nm)" package="0805 [SMD]"]
  LED6 = smd LED [color="Red (633nm)" package="0805 [SMD]"]
  LED7 = smd LED [color="Red (633nm)" package="0805 [SMD]"]
  LED8 = smd LED [color="Red (633nm)" package="0805 [SMD]"]

nets:
  N1: Componente2.3V3, LED1.cathode, LED2.cathode, LED3.cathode, LED4.cathode, LED5.cathode, LED6.cathode, LED7.cathode, LED8.cathode
  N2: Componente2.GND, SW1.9, SW1.10, SW1.11, SW1.12, SW1.13, SW1.14, SW1.15, SW1.16, SW2.12, SW2.13, SW2.14, SW2.15, SW2.16, R1.Pin_0, R2.Pin_0, R3.Pin_0, R4.Pin_0, R5.Pin_0, R6.Pin_0, R7.Pin_0, R8.Pin_0, R9.Pin_0, R10.Pin_0, R11.Pin_0, R12.Pin_0, R13.Pin_0
  N3: Componente2.D23, SW1.1, R1.Pin_1
  N4: Componente2.D25, SW1.2, R2.Pin_1
  N5: Componente2.D27, SW1.3, R3.Pin_1
  N6: Componente2.D29, SW1.4, R4.Pin_1
  N7: Componente2.D31, SW1.5, R5.Pin_1
  N8: Componente2.D33, SW1.6, R6.Pin_1
  N9: Componente2.D34, LED1.anode
  N10: Componente2.D35, SW1.7, R7.Pin_1
  N11: Componente2.D36, LED2.anode
  N12: Componente2.D37, SW1.8, R8.Pin_1
  N13: Componente2.D38, LED3.anode
  N14: Componente2.D39, SW2.1, R9.Pin_1
  N15: Componente2.D40, LED4.anode
  N16: Componente2.D41, SW2.2, R10.Pin_1
  N17: Componente2.D42, LED5.anode
  N18: Componente2.D43, SW2.3, R11.Pin_1
  N19: Componente2.D44, LED6.anode
  N20: Componente2.D45, SW2.4, R12.Pin_1
  N21: Componente2.D46, LED7.anode
  N22: Componente2.D47, SW2.5, R13.Pin_1
  N23: Componente2.D48, LED8.anode
